# Fritzing sketch Beat707 NXT V1-Arduino-Mini (saved by Fritzing 0.9.3b)
circuit board: 10cm x 4.9cm
breadboards: 1

parts:
  47uF = Electrolytic Capacitor [capacitance=47µF package="100 mil [THT, electrolytic]"]
  10k = Resistor [tolerance=±5% resistance=10k package=THT]
  MIDI_Output = MIDI_CONN_FEMALE_SUPPORT [part_number="MIDI Output" package=din_5_female_support]
  W25Q64 = IC, DIP package, 8 pins [chip_label=Flash part_number="W25Q64 (Winbond)"]
  Main_Header = male pin header, 7 pins [form="♂ (male)"]
  33 = Resistor [tolerance=±5% resistance=33 package=THT]
  4N35 = Optocoupler [package=THT]
  1N4748 = Rectifier Diode [part_number=1N4748 package="300 mil [THT]"]
  MIDI_Input = MIDI_CONN_FEMALE_SUPPORT [part_number="MIDI Input" package=din_5_female_support]
  1k = Resistor [tolerance=±5% resistance=1k package=THT]
  220 = Resistor [tolerance=±5% resistance=220 part_number=O1 package=THT]
  Arduino-Mini-Pro_3_3V = Arduino Pro Mini v13
  LD33V = LD33 Low-Dropout Voltage Regulator [part_number=LD33V]
  47uF2 = Electrolytic Capacitor [capacitance=47µF package="100 mil [THT, electrolytic]"]
  10 = Resistor [tolerance=±5% resistance=10 package=THT]
  C1 = Ceramic Capacitor [capacitance=100nF package="100 mil [THT, multilayer]"]

nets (from the pcb view):
  N1: 47uF.-, MIDI_Output.NC1, Main_Header.pin1, MIDI_Input.NC1, 1k.Pin_1, LD33V.Vin, 47uF2.+
  N2: 47uF.+, 10k.Pin_1, W25Q64.pin3, W25Q64.pin7, W25Q64.pin8, LD33V.Vout, 10.Pin_0, C1.1
  N3: 10k.Pin_0, Arduino-Mini-Pro_3_3V.RESET
  N4: MIDI_Output.NC2, MIDI_Output.MIDI_IN, 33.Pin_0
  N5: MIDI_Output.MIDI_OUT, 10.Pin_1
  N6: W25Q64.pin4, Main_Header.pin2, 4N35.Pin_6, LD33V.GND, 47uF2.-, C1.0
  N7: 4N35.Pin_1, 1N4748.cathode, 220.Pin_1
  N8: 4N35.Pin_2, 1N4748.anode, MIDI_Input.MIDI_IN
  N9: 4N35.Pin_5, 1k.Pin_0
  N10: MIDI_Input.MIDI_OUT, 220.Pin_0

notes:
  GND
  Beat707.com (c) 2017
  Wusik.com
  Kalfelz.com
  V1
  5V
  Beat707 NXT
  3.3V
  47uF
  MIDI-IN
  MIDI-OUT
